# Fritzing sketch mk61avr (saved by Fritzing 0.9.0b)
circuit board: 13.9235cm x 14.0858cm
breadboards: 1
perfboards: 1

parts:
  R1 = Resistor [tolerance=±5% resistance=220 package=THT]
  9 = Momentary Switch [package=ksa_sealed_tac_switch]
  SS = Momentary Switch [package=ksa_sealed_tac_switch]
  Sub = Momentary Switch [package=ksa_sealed_tac_switch]
  Store = Momentary Switch [package=ksa_sealed_tac_switch]
  Goto = Momentary Switch [package=ksa_sealed_tac_switch]
  U1 = LCD-16X2 [package=lcd-16x2]
  D3 = Diode [package=diode-1n4001]
  POW = Momentary Switch [package=ksa_sealed_tac_switch]
  <- = Momentary Switch [package=ksa_sealed_tac_switch]
  x = Momentary Switch [package=ksa_sealed_tac_switch]
  Load = Momentary Switch [package=ksa_sealed_tac_switch]
  VCC1 = Battery
  On/Off = Momentary Switch [package=ksa_sealed_tac_switch]
  F = Momentary Switch [package=ksa_sealed_tac_switch]
  XY = Momentary Switch [package=ksa_sealed_tac_switch]
  Cx = Momentary Switch [package=ksa_sealed_tac_switch]
  7 = Momentary Switch [package=ksa_sealed_tac_switch]
  / = Momentary Switch [package=ksa_sealed_tac_switch]
  Step-> = Momentary Switch [package=ksa_sealed_tac_switch]
  D7 = Diode [package=diode-1n4001]
  Load_2 = Momentary Switch [package=ksa_sealed_tac_switch]
  8 = Momentary Switch [package=ksa_sealed_tac_switch]
  - = Momentary Switch [package=ksa_sealed_tac_switch]
  0 = Momentary Switch [package=ksa_sealed_tac_switch]
  6 = Momentary Switch [package=ksa_sealed_tac_switch]
  D1 = Diode [package=diode-1n4001]
  Ret = Momentary Switch [package=ksa_sealed_tac_switch]
  R4 = Resistor [tolerance=±5% resistance=220 package=THT]
  -> = Momentary Switch [package=ksa_sealed_tac_switch]
  3 = Momentary Switch [package=ksa_sealed_tac_switch]
  2 = Momentary Switch [package=ksa_sealed_tac_switch]
  D10 = Diode [package=diode-1n4001]
  D6 = Diode [package=diode-1n4001]
  1 = Momentary Switch [package=ksa_sealed_tac_switch]
  D8 = Diode [package=diode-1n4001]
  D4 = Diode [package=diode-1n4001]
  IC1 = MICROCONTROLLER [package=dil28-3]
  D2 = Diode [package=diode-1n4001]
  4 = Momentary Switch [package=ksa_sealed_tac_switch]
  D5 = Diode [package=diode-1n4001]
  /-/ = Momentary Switch [package=ksa_sealed_tac_switch]
  D9 = Diode [package=diode-1n4001]
  + = Momentary Switch [package=ksa_sealed_tac_switch]
  Save = Momentary Switch [package=ksa_sealed_tac_switch]
  K = Momentary Switch [package=ksa_sealed_tac_switch]
  Bx = Momentary Switch [package=ksa_sealed_tac_switch]
  R2 = Resistor [tolerance=±5% resistance=220 package=THT]
  R3 = Resistor [tolerance=±5% resistance=220 package=THT]
  S2 = Momentary Switch [package=ksa_sealed_tac_switch]
  part = Momentary Switch [package=ksa_sealed_tac_switch]
  Step<- = Momentary Switch [package=ksa_sealed_tac_switch]
  5 = Momentary Switch [package=ksa_sealed_tac_switch]
  JP1 = Header 5x2 [package=2x5-shrouded_smd]

nets:
  N1: R1.Pin_0, <-.3, On/Off.3
  N2: R1.Pin_1, IC1.PD3(INT1)
  N3: 9.1, D1.A
  N4: 9.2, Bx.1
  N5: 9.4, 8.4
  N6: SS.1, SS.4, Sub.1, Sub.2, Sub.3, Sub.4, Store.3, Store.4, Goto.1, Goto.2, Goto.3, Goto.4, POW.2, POW.4, x.2, x.4, F.1, F.2, XY.4, Cx.4, /.2, /.4, Step->.1, Step->.2, Step->.3, Step->.4, Load_2.3, Load_2.4, -.2, -.4, Ret.1, Ret.3, Ret.4, /-/.4, +.2, K.3, Bx.2, part.2, part.4, Step<-.1, Step<-.2, Step<-.3, Step<-.4
  N7: SS.3, R4.Pin_0, +.4, R3.Pin_0
  N8: Store.1, XY.2
  VSS: U1.VSS, U1.VO, VCC1.-, IC1.GND, IC1.AGND, S2.3, S2.4, JP1.4, JP1.6, JP1.8, JP1.10
  VDD: U1.VDD, VCC1.+, IC1.VCC, IC1.AVCC
  N9: U1.RS, IC1.PD5(T1)
  N10: U1.R_W, IC1.PD6(AIN0)
  N11: U1.E, IC1.PD7(AIN1)
  N12: U1.DB4, IC1.PC0(ADC0)
  N13: U1.DB5, IC1.PC1(ADC1)
  N14: U1.DB6, IC1.PC2(ADC2)
  N15: U1.DB7, IC1.PC3(ADC3)
  N16: D3.A, <-.1
  N17: D3.C, IC1.PB1(OC1A)
  N18: POW.1, 7.2
  N19: POW.3, /-/.3
  N20: <-.2, 1.1
  N21: <-.4, ->.4
  N22: x.1, 2.2
  N23: x.3, /.3
  N24: Load.1, D6.A
  N25: Load.2, 4.1
  N26: Load.4, Save.4
  N27: On/Off.1, D2.A
  N28: On/Off.2, 0.1
  N29: F.3, F.4, Load_2.1, /-/.2, K.4, Bx.4
  N30: XY.1, 4.2
  N31: XY.3, part.3
  N32: Cx.1, 8.2
  N33: Cx.2, K.1
  N34: Cx.3, Bx.3
  N35: 7.1, D9.A
  N36: 7.3, 8.3
  N37: 7.4, 6.4
  N38: /.1, 3.2
  N39: D7.A, 5.1
  N40: D7.C, IC1.PB5(SCK), JP1.7
  N41: 8.1, D10.A
  N42: -.1, 1.2
  N43: -.3, +.3
  N44: 0.2, +.1
  N45: 0.3, R2.Pin_0
  N46: 0.4, 1.4
  N47: 6.1, D8.A
  N48: 6.2, /-/.1
  N49: 6.3, 5.3
  N50: D1.C, IC1.PC5(ADC5_SCL)
  N51: R4.Pin_1, IC1.PD0(RXD)
  N52: ->.1, D4.A
  N53: ->.2, 2.1
  N54: ->.3, Save.3
  N55: 3.1, Save.2
  N56: 3.3, 4.3
  N57: 3.4, 2.4
  N58: 2.3, 1.3
  N59: D10.C, IC1.PC4(ADC4_SDA)
  N60: D6.C, IC1.PB4(MISO), JP1.9
  N61: D8.C, IC1.PB6(XTAL1_TOSC1)
  N62: D4.C, IC1.PB2(SS_OC1B)
  N63: IC1.PC6(_RESET), S2.1, S2.2, JP1.5
  N64: IC1.PD1(TXD), R3.Pin_1
  N65: IC1.PD2(INT0), R2.Pin_1
  N66: IC1.PB7(XTAL2_TOSC2), D9.C
  N67: IC1.PB0(ICP), D2.C
  N68: IC1.PB3(MOSI_OC2), D5.C, JP1.1, JP1.3
  N69: 4.4, 5.4
  N70: D5.A, Save.1
  N71: part.1, 5.2

notes:
  Столбцы клавиатуры - PB0-7 и PC4-5 (10 шт)
  Строки клавиатуры - PD0-3 (4шт)
