# Fritzing sketch mk61avr_I2C (saved by Fritzing 0.9.0b)
circuit board: 13.9235cm x 14.0858cm
breadboards: 1
perfboards: 1

parts:
  R1 = Resistor [tolerance=±5% resistance=220 package=THT]
  9 = Momentary Switch [package=ksa_sealed_tac_switch]
  SS = Momentary Switch [package=ksa_sealed_tac_switch]
  Sub = Momentary Switch [package=ksa_sealed_tac_switch]
  Store = Momentary Switch [package=ksa_sealed_tac_switch]
  Goto = Momentary Switch [package=ksa_sealed_tac_switch]
  U1 = LCD-16X2 [package=lcd-16x2]
  D3 = Diode [package=diode-1n4001]
  POW = Momentary Switch [package=ksa_sealed_tac_switch]
  <- = Momentary Switch [package=ksa_sealed_tac_switch]
  x = Momentary Switch [package=ksa_sealed_tac_switch]
  Load = Momentary Switch [package=ksa_sealed_tac_switch]
  VCC1 = Battery
  F = Momentary Switch [package=ksa_sealed_tac_switch]
  XY = Momentary Switch [package=ksa_sealed_tac_switch]
  Cx = Momentary Switch [package=ksa_sealed_tac_switch]
  7 = Momentary Switch [package=ksa_sealed_tac_switch]
  / = Momentary Switch [package=ksa_sealed_tac_switch]
  Step-> = Momentary Switch [package=ksa_sealed_tac_switch]
  D7 = Diode [package=diode-1n4001]
  Load_2 = Momentary Switch [package=ksa_sealed_tac_switch]
  8 = Momentary Switch [package=ksa_sealed_tac_switch]
  - = Momentary Switch [package=ksa_sealed_tac_switch]
  0 = Momentary Switch [package=ksa_sealed_tac_switch]
  6 = Momentary Switch [package=ksa_sealed_tac_switch]
  D1 = Diode [package=diode-1n4001]
  Ret = Momentary Switch [package=ksa_sealed_tac_switch]
  R4 = Resistor [tolerance=±5% resistance=220 package=THT]
  -> = Momentary Switch [package=ksa_sealed_tac_switch]
  3 = Momentary Switch [package=ksa_sealed_tac_switch]
  2 = Momentary Switch [package=ksa_sealed_tac_switch]
  D10 = Diode [package=diode-1n4001]
  D6 = Diode [package=diode-1n4001]
  1 = Momentary Switch [package=ksa_sealed_tac_switch]
  D8 = Diode [package=diode-1n4001]
  D4 = Diode [package=diode-1n4001]
  IC1 = MICROCONTROLLER [package=dil28-3]
  D2 = Diode [package=diode-1n4001]
  4 = Momentary Switch [package=ksa_sealed_tac_switch]
  D5 = Diode [package=diode-1n4001]
  /-/ = Momentary Switch [package=ksa_sealed_tac_switch]
  D9 = Diode [package=diode-1n4001]
  + = Momentary Switch [package=ksa_sealed_tac_switch]
  Save = Momentary Switch [package=ksa_sealed_tac_switch]
  K = Momentary Switch [package=ksa_sealed_tac_switch]
  Bx = Momentary Switch [package=ksa_sealed_tac_switch]
  R2 = Resistor [tolerance=±5% resistance=220 package=THT]
  R3 = Resistor [tolerance=±5% resistance=220 package=THT]
  S2 = Momentary Switch [package=ksa_sealed_tac_switch]
  part = Momentary Switch [package=ksa_sealed_tac_switch]
  Step<- = Momentary Switch [package=ksa_sealed_tac_switch]
  5 = Momentary Switch [package=ksa_sealed_tac_switch]
  JP1 = Header 5x2 [package=2x5-shrouded_smd]
  LCM1602_IIC1 = LCM1602 IIC [part_number="LCM1602 IIC" chip_label="LCM1602 IIC" package="DIP (Dual Inline) [THT]"]
  X1 = DB9 Connector [package=db9]
  On/Off = Momentary Switch [package=ksa_sealed_tac_switch]

nets (from the breadboard view):
  N1: R1.Pin_0, <-.3, On/Off.3
  N2: R1.Pin_1, IC1.PD5(T1)
  N3: 9.1, D1.A
  N4: 9.2, Bx.1
  N5: 9.4, 8.4
  N6: SS.1, SS.4, Sub.1, Sub.2, Sub.3, Sub.4, Store.3, Store.4, Goto.1, Goto.2, Goto.3, Goto.4, POW.2, POW.4, x.2, x.4, F.1, F.2, XY.4, Cx.4, /.2, /.4, Step->.1, Step->.2, Step->.3, Step->.4, Load_2.3, Load_2.4, -.2, -.4, Ret.1, Ret.3, Ret.4, /-/.4, +.2, K.3, Bx.2, part.2, part.4, Step<-.1, Step<-.2, Step<-.3, Step<-.4
  N7: SS.3, R4.Pin_0, +.4, R3.Pin_0
  N8: Store.1, XY.2
  VSS: U1.VSS, LCM1602_IIC1.VSS
  VDD: U1.VDD, LCM1602_IIC1.VDD
  N9: U1.VO, LCM1602_IIC1.V0
  N10: U1.RS, LCM1602_IIC1.RS
  N11: U1.R_W, LCM1602_IIC1.RW
  N12: U1.E, LCM1602_IIC1.E
  N13: U1.DB0, LCM1602_IIC1.D0
  N14: U1.DB1, LCM1602_IIC1.D1
  N15: U1.DB2, LCM1602_IIC1.D2
  N16: U1.DB3, LCM1602_IIC1.D3
  N17: U1.DB4, LCM1602_IIC1.D4
  N18: U1.DB5, LCM1602_IIC1.D5
  N19: U1.DB6, LCM1602_IIC1.D6
  N20: U1.DB7, LCM1602_IIC1.D7
  N21: U1.A, LCM1602_IIC1.A
  N22: U1.K, LCM1602_IIC1.K
  N23: D3.A, <-.1
  N24: D3.C, IC1.PB1(OC1A)
  N25: POW.1, 7.2
  N26: POW.3, /-/.3
  N27: <-.2, 1.1
  N28: <-.4, ->.4
  N29: x.1, 2.2
  N30: x.3, /.3
  N31: Load.1, D6.A
  N32: Load.2, 4.1
  N33: Load.4, Save.4
  GND: VCC1.-, IC1.GND, IC1.AGND, S2.3, S2.4, JP1.4, JP1.6, JP1.8, JP1.10, LCM1602_IIC1.GND, X1.5
  VCC: VCC1.+, IC1.VCC, IC1.AVCC, LCM1602_IIC1.VCC
  N34: F.3, F.4, Load_2.1, /-/.2, K.4, Bx.4
  N35: XY.1, 4.2
  N36: XY.3, part.3
  N37: Cx.1, 8.2
  N38: Cx.2, K.1
  N39: Cx.3, Bx.3
  N40: 7.1, D9.A
  N41: 7.3, 8.3
  N42: 7.4, 6.4
  N43: /.1, 3.2
  N44: D7.A, 5.1
  N45: D7.C, IC1.PB5(SCK), JP1.7
  N46: 8.1, D10.A
  N47: -.1, 1.2
  N48: -.3, +.3
  N49: 0.1, On/Off.2
  N50: 0.2, +.1
  N51: 0.3, R2.Pin_0
  N52: 0.4, 1.4
  N53: 6.1, D8.A
  N54: 6.2, /-/.1
  N55: 6.3, 5.3
  N56: D1.C, IC1.PC1(ADC1)
  N57: R4.Pin_1, IC1.PD2(INT0)
  N58: ->.1, D4.A
  N59: ->.2, 2.1
  N60: ->.3, Save.3
  N61: 3.1, Save.2
  N62: 3.3, 4.3
  N63: 3.4, 2.4
  N64: 2.3, 1.3
  N65: D10.C, IC1.PC0(ADC0)
  N66: D6.C, IC1.PB4(MISO), JP1.9
  N67: D8.C, IC1.PB6(XTAL1_TOSC1)
  N68: D4.C, IC1.PB2(SS_OC1B)
  N69: IC1.PC6(_RESET), S2.1, S2.2, JP1.5
  N70: IC1.PD0(RXD), X1.8
  N71: IC1.PD1(TXD), X1.7
  N72: IC1.PD3(INT1), R3.Pin_1
  N73: IC1.PD4(XCK_T0), R2.Pin_1
  N74: IC1.PB7(XTAL2_TOSC2), D9.C
  N75: IC1.PB0(ICP), D2.C
  N76: IC1.PB3(MOSI_OC2), D5.C, JP1.1, JP1.3
  N77: IC1.PC4(ADC4_SDA), LCM1602_IIC1.SDA
  N78: IC1.PC5(ADC5_SCL), LCM1602_IIC1.SCL
  N79: D2.A, On/Off.1
  N80: 4.4, 5.4
  N81: D5.A, Save.1
  N82: part.1, 5.2
  N83: LCM1602_IIC1.LED_A, LCM1602_IIC1.LED_B

notes:
  Столбцы клавиатуры - PB0-7 и PC0-1 (10 шт)
  Строки клавиатуры - PD2-5 (4шт)

custom parts:
  LCM1602 IIC: I2C-Module to use a 1602 or 2004 LCD on with the wire.h libory Serial LCD Modul
